// Digital circuit 32位计算机.dig as structural Verilog
module \_32位计算机  (
  input  Clock,
  output [31:0] out_2
);

  wire add_1_c_o, and_3_out, clock_t, comparator_1_eq, comparator_2_eq, comparator_3_eq, CS_RAM, CS_ROM,
       CS_S, DN_SP, driverinvsel_1_out, END_CYCLE, Flag_c, Flag_z, HALT, INC_PC, LD_IR, LD_MAR, LD_MDREXT,
       LD_MDRINT, LD_PC, LD_RFlags, LD_Rw, LD_SP, multiplexer_1_out, multiplexer_3_out, not_1_out, not_3_out,
       not_4_out, not_5_out, OE, OE_ALU, OE_MDREXT, OE_MDRINT, OE_PC, OE_Ra, OE_Rb, OE_SP, or_1_out,
       sub_1_c_o, UP_SP, WE;
  wire [3:0] ADDR_Ra, ADDR_Rb, ADDR_Rw, MODE_ALU, STATE_out;
  wire [25:17] CU_d;
  wire [31:0] add_1_s, and_2_out, barrelshifter_1_out, DEC_s, div_1_q, div_1_r, driver_1_out, driver_7_out,
       INC_s, IR_q, MAR_q, MDR_EXT_q, MDR_INT_q, multiplexer_2_out, nand_1_out, nor_1_out, not_2_out,
       or_3_out, RegFile_da, RegFile_db, SP_out, sub_1_s, xnor_1_out, xor_1_out;
  wire [63:0] mul_1_mul;

  CounterPreset #(.Bits(32), .isProgramCounter("true")) PC (
    .en(INC_PC), .C(clock_t), .dir(1'b0), .in(driver_1_out), .ld(LD_PC), .clr(1'b0), .out(out_2));  // open: ovf
  not not_1 (not_1_out, HALT);
  and and_1 (clock_t, Clock, not_1_out);
  assign driver_1_out = OE_PC ? out_2 : 32'bz;  // Driver driver_1
  CounterPreset #(.maxValue(15), .Bits(4)) STATE (
    .en(1'b1), .C(clock_t), .dir(1'b0), .in(4'b0000), .ld(1'b0), .clr(END_CYCLE), .out(STATE_out));  // open: ovf
  Register #(.Bits(32)) IR (
    .D(driver_1_out), .C(clock_t), .en(LD_IR), .Q({IR_q[31:20], ADDR_Ra, ADDR_Rb, ADDR_Rw, IR_q[7:0]}));
  Comparator #(.Bits(8)) u_HALT (.a(IR_q[7:0]), .b(8'hf0), .eq(HALT));  // open: gt, lt
  assign driver_1_out = OE_Ra ? RegFile_da : 32'bz;  // Driver driver_2
  RegisterFile #(.AddrBits(4), .Bits(32)) RegFile (
    .Din(driver_1_out), .we(LD_Rw), .Rw(ADDR_Rw), .C(clock_t), .Ra(ADDR_Ra), .Rb(ADDR_Rb), .Da(RegFile_da),
    .Db(RegFile_db));
  assign driver_1_out = OE_Rb ? RegFile_db : 32'bz;  // Driver driver_3
  or or_1 (or_1_out, DN_SP, UP_SP);
  CounterPreset #(.Bits(32)) SP (
    .en(or_1_out), .C(clock_t), .dir(DN_SP), .in(driver_1_out), .ld(LD_SP), .clr(1'b0), .out(SP_out));  // open: ovf
  assign driver_1_out[0] = OE_SP ? SP_out[0] : 1'bz;  // Driver driver_4
  Comparator #(.Bits(8)) comparator_1 (.a(IR_q[7:0]), .b(8'h33), .eq(comparator_1_eq));  // open: gt, lt
  ROM #(.AddrBits(12), .isProgramMemory("true"), .Bits(26)) CU (
    .A({IR_q[7:0], STATE_out}), .sel(1'b1),
    .D({CU_d[25:24], MODE_ALU, WE, OE, CU_d[17], OE_ALU, OE_Rb, OE_Ra, OE_MDREXT, OE_MDRINT, OE_PC, OE_SP, LD_RFlags, LD_Rw, LD_IR, LD_MDREXT, LD_MDRINT, LD_MAR, LD_PC, LD_SP, UP_SP, DN_SP}));
  assign driver_1_out = OE_ALU ? multiplexer_2_out : 32'bz;  // Driver driver_5
  assign driverinvsel_1_out = ~comparator_1_eq ? and_3_out : 1'bz;  // DriverInvSel driverinvsel_1
  or or_2 (INC_PC, CU_d[17], driverinvsel_1_out);
  Add #(.Bits(32)) add_1 (.a(RegFile_da), .b(RegFile_db), .c_i(1'b0), .s(add_1_s), .c_o(add_1_c_o));
  Sub #(.Bits(32)) sub_1 (.a(RegFile_da), .b(RegFile_db), .c_i(1'b0), .s(sub_1_s), .c_o(sub_1_c_o));
  Mul #(.Bits(32)) mul_1 (.a(RegFile_da), .b(RegFile_db), .mul(mul_1_mul));
  Div #(.Bits(32)) div_1 (.a(RegFile_da), .b(RegFile_db), .q(div_1_q), .r(div_1_r));
  BarrelShifter #(.Bits(32)) barrelshifter_1 (.in(RegFile_da), .shift(RegFile_db[5:0]), .out(barrelshifter_1_out));
  assign and_2_out = RegFile_da & RegFile_db;  // And and_2, 32 bits wide
  assign nand_1_out = ~(RegFile_da & RegFile_db);  // NAnd nand_1, 32 bits wide
  assign or_3_out = RegFile_da | RegFile_db;  // Or or_3, 32 bits wide
  assign nor_1_out = ~(RegFile_da | RegFile_db);  // NOr nor_1, 32 bits wide
  assign xor_1_out = RegFile_da ^ RegFile_db;  // XOr xor_1, 32 bits wide
  assign xnor_1_out = ~(RegFile_da ^ RegFile_db);  // XNOr xnor_1, 32 bits wide
  assign not_2_out = ~RegFile_da;  // Not not_2, 32 bits wide
  Add #(.Bits(32)) INC (.a(RegFile_da), .b(32'h1), .c_i(1'b0), .s(INC_s));  // open: c_o
  Sub #(.Bits(32)) DEC (.a(RegFile_da), .b(32'h1), .c_i(1'b0), .s(DEC_s));  // open: c_o
  or or_4 (END_CYCLE, and_3_out, CU_d[25]);
  Multiplexer #(.Selector_Bits(4)) multiplexer_1 (
    .sel(IR_q[23:20]), .in_0(1'b0), .in_1(Flag_c), .in_2(Flag_z), .in_3(not_3_out), .in_4(not_4_out),
    .in_5(1'b0), .in_6(1'b0), .in_7(1'b0), .in_8(1'b0), .in_9(1'b0), .in_10(1'b0), .in_11(1'b0),
    .in_12(1'b0), .in_13(1'b0), .in_14(1'b0), .in_15(1'b0), .out(multiplexer_1_out));
  not not_3 (not_3_out, Flag_c);
  not not_4 (not_4_out, Flag_z);
  not not_5 (not_5_out, multiplexer_1_out);
  and and_3 (and_3_out, CU_d[24], not_5_out);
  assign driver_1_out = OE_MDRINT ? MDR_INT_q : 32'bz;  // Driver driver_6
  Register #(.Bits(32)) MDR_EXT (.D(driver_1_out), .C(clock_t), .en(LD_MDREXT), .Q(MDR_EXT_q));
  Register #(.Bits(32)) MDR_INT (.D(driver_7_out), .C(clock_t), .en(LD_MDRINT), .Q(MDR_INT_q));
  assign driver_7_out = OE_MDREXT ? MDR_EXT_q : 32'bz;  // Driver driver_7
  Multiplexer #(.Selector_Bits(4), .Bits(32)) multiplexer_2 (
    .sel(MODE_ALU), .in_0(add_1_s), .in_1(sub_1_s), .in_2(mul_1_mul[31:0]), .in_3(div_1_q),
    .in_4(barrelshifter_1_out), .in_5(and_2_out), .in_6(nand_1_out), .in_7(or_3_out), .in_8(nor_1_out),
    .in_9(xor_1_out), .in_10(xnor_1_out), .in_11(not_2_out), .in_12(INC_s), .in_13(DEC_s), .in_14(div_1_r),
    .in_15({32{1'b0}}), .out(multiplexer_2_out));
  Register #(.Bits(32)) MAR (.D(driver_1_out), .C(clock_t), .en(LD_MAR), .Q(MAR_q));
  Comparator #(.Bits(32)) comparator_2 (.a({32{1'b0}}), .b(multiplexer_2_out), .eq(comparator_2_eq));  // open: gt, lt
  Multiplexer multiplexer_3 (.sel(comparator_3_eq), .in_0(add_1_c_o), .in_1(sub_1_c_o), .out(multiplexer_3_out));
  Comparator #(.Bits(4)) comparator_3 (.a(MODE_ALU), .b(4'b0001), .eq(comparator_3_eq));  // open: gt, lt
  Register register_1 (.D(comparator_2_eq), .C(clock_t), .en(LD_RFlags), .Q(Flag_z));
  Register register_2 (.D(multiplexer_3_out), .C(clock_t), .en(LD_RFlags), .Q(Flag_c));
  Decoder #(.Selector_Bits(4)) decoder_1 (
    .sel(MAR_q[27:24]), .out_0(CS_ROM), .out_1(CS_RAM), .out_2(CS_S));  // open: out_3, out_4, out_5, out_6, out_7, out_8, out_9, out_10, out_11, out_12, out_13, out_14, out_15
  EEPROM #(.AddrBits(24), .Bits(32)) ROM (.A(MAR_q[23:0]), .CS(CS_ROM), .WE(1'b0), .OE(OE), .D(driver_7_out));
  RAMSinglePortSel #(.AddrBits(24), .Bits(32)) RAM (.A(MAR_q[23:0]), .CS(CS_RAM), .WE(WE), .OE(OE), .D(driver_7_out));
  RAMSinglePortSel #(.AddrBits(24), .Bits(32)) Stack (.A(MAR_q[23:0]), .CS(CS_S), .WE(WE), .OE(OE), .D(driver_7_out));
  // Pins of 1 and 32 bits meet at driver_1_out
  // Pins of 1 and 32 bits meet at SP_out

  // Notes on the sheet:
  //   Clock: Hz: 65536
  //   ALU
  //   contents of CU (hex, n*v repeats v):
  //   f0082,f6004,f0110,2f0000,12*0,f0082,f6004,f0110,2f0000,12*0,f0082
  //   ,f6004,f0110,2f0000,12*0,f0082,f6004,f0110,2f0000,12*0,f0082,f6004
  //   ,f0110,2f0000,12*0,f0082,f6004,f0110,2f0000,12*0,f0082,f6004,f0110
  //   ,2f0000,12*0,f0082,f6004,f0110,2f0000,12*0,f0082,f6004,f0110,2f0000
  //   ,12*0,f0082,f6004,f0110,2f0000,12*0,f0082,f6004,f0110,2f0000,12*0
  //   ,f0082,f6004,f0110,2f0000,12*0,f0082,f6004,f0110,2f0000,12*0,f0082
  //   ,f6004,f0110,2f0000,12*0,f0082,f6004,f0110,2f0000,12*0,f0082,f6004
  //   ,f0110,2f0000,12*0,f0082,f6004,f0110,2f0420,12*0,f0082,f6004,f0110
  //   ,f0802,f4004,2f0120,10*0,f0082,f6004,f0110,f0802,f0408,2f8200
  //   ,10*0,f0082,f6004,f0110,f0082,f6004,f0102,f4004,2f0120,8*0,f0082
  //   ,f6004,f0110,f0082,f6004,f0102,f0408,2f8200,8*0,f0082,f6004,f0110
  //   ,f2082,f4004,2f0120,10*0,f0082,f6004,f0110,f2082,f4004,2f0120
  //   ,10*0,f0082,f6004,f0110,1002,f4004,2f0120,10*0,f0082,f6004,f0110
  //   ,2f0000,12*0,f0082,f6004,f0110,2f0000,12*0,f0082,f6004,f0110,2f0000
  //   ,12*0,f0082,f6004,f0110,2f0000,12*0,f0082,f6004,f0110,2f0000,12*0
  //   ,f0082,f6004,f0110,2f0000,12*0,f0082,f6004,f0110,2f0000,12*0,f0082
  //   ,f6004,f0110,2f0000,12*0,f0082,f6004,f0110,201060,12*0,f0082,f6004
  //   ,f0110,211060,12*0,f0082,f6004,f0110,2c1020,12*0,f0082,f6004,f0110
  //   ,2d1020,12*0,f0082,f6004,f0110,221060,12*0,f0082,f6004,f0110,231060
  //   ,12*0,f0082,f6004,f0110,2e1060,12*0,f0082,f6004,f0110,241060,12*0
  //   ,f0082,f6004,f0110,251060,12*0,f0082,f6004,f0110,261060,12*0,f0082
  //   ,f6004,f0110,271060,12*0,f0082,f6004,f0110,281060,12*0,f0082,f6004
  //   ,f0110,291060,12*0,f0082,f6004,f0110,2a1060,12*0,f0082,f6004,f0110
  //   ,2b1060,12*0,f0082,f6004,f0110,211040,12*0,f0082,f6004,f0110,f0082
  //   ,f6004,2f0101,10*0,f0082,f6004,f0110,100000,f0082,f6004,2f0101
  //   ,9*0,f0082,f6004,f0110,2f0401,12*0,f0082,f6004,f0110,100000,2f0401
  //   ,11*0,f0082,f6004,f0110,f2082,f4004,f0402,f0088,f8200,c1020,3e0101
  //   ,6*0,f0082,f6004,f0110,100000,f2082,f4004,f0402,f0088,f8200,c1020
  //   ,3e0101,5*0,f0082,f6004,f0110,d1020,f0402,f4004,2f0101,9*0,f0082
  //   ,f6004,f0110,2f0000,12*0,f0082,f6004,f0110,2f0000,12*0,f0082,f6004
  //   ,f0110,2f0000,12*0,f0082,f6004,f0110,2f0000,12*0,f0082,f6004,f0110
  //   ,2f0000,12*0,f0082,f6004,f0110,2f0000,12*0,f0082,f6004,f0110,2f0000
  //   ,12*0,f0082,f6004,f0110,2f0000,12*0,f0082,f6004,f0110,2f0000,12*0
  //   ,f0082,f6004,f0110,2f0000,12*0,f0082,f6004,f0110,2f0000,12*0,f0082
  //   ,f6004,f0110,2f0000,12*0,f0082,f6004,f0110,2f0000,12*0,f0082,f6004
  //   ,f0110,2f0000,12*0,f0082,f6004,f0110,2f0000,12*0,f0082,f6004,f0110
  //   ,2f0000,12*0,f0082,f6004,f0110,2f0000,12*0,f0082,f6004,f0110,2f0000
  //   ,12*0,f0082,f6004,f0110,2f0000,12*0,f0082,f6004,f0110,2f0000,12*0
  //   ,f0082,f6004,f0110,2f0000,12*0,f0082,f6004,f0110,2f0000,12*0,f0082
  //   ,f6004,f0110,2f0000,12*0,f0082,f6004,f0110,2f0000,12*0,f0082,f6004
  //   ,f0110,2f0000,12*0,f0082,f6004,f0110,2f0000,12*0,f0082,f6004,f0110
  //   ,2f0000,12*0,f0082,f6004,f0110,2f0000,12*0,f0082,f6004,f0110,2f0000
  //   ,12*0,f0082,f6004,f0110,2f0000,12*0,f0082,f6004,f0110,2f0000,12*0
  //   ,f0082,f6004,f0110,2f0000,12*0,f0082,f6004,f0110,2f0000,12*0,f0082
  //   ,f6004,f0110,2f0000,12*0,f0082,f6004,f0110,2f0000,12*0,f0082,f6004
  //   ,f0110,2f0000,12*0,f0082,f6004,f0110,2f0000,12*0,f0082,f6004,f0110
  //   ,2f0000,12*0,f0082,f6004,f0110,2f0000,12*0,f0082,f6004,f0110,2f0000
  //   ,12*0,f0082,f6004,f0110,2f0000,12*0,f0082,f6004,f0110,2f0000,12*0
  //   ,f0082,f6004,f0110,2f0000,12*0,f0082,f6004,f0110,2f0000,12*0,f0082
  //   ,f6004,f0110,2f0000,12*0,f0082,f6004,f0110,2f0000,12*0,f0082,f6004
  //   ,f0110,2f0000,12*0,f0082,f6004,f0110,2f0000,12*0,f0082,f6004,f0110
  //   ,2f0000,12*0,f0082,f6004,f0110,2f0000,12*0,f0082,f6004,f0110,2f0000
  //   ,12*0,f0082,f6004,f0110,2f0000,12*0,f0082,f6004,f0110,2f0000,12*0
  //   ,f0082,f6004,f0110,2f0000,12*0,f0082,f6004,f0110,2f0000,12*0,f0082
  //   ,f6004,f0110,2f0000,12*0,f0082,f6004,f0110,2f0000,12*0,f0082,f6004
  //   ,f0110,2f0000,12*0,f0082,f6004,f0110,2f0000,12*0,f0082,f6004,f0110
  //   ,2f0000,12*0,f0082,f6004,f0110,2f0000,12*0,f0082,f6004,f0110,2f0000
  //   ,12*0,f0082,f6004,f0110,2f0000,12*0,f0082,f6004,f0110,2f0000,12*0
  //   ,f0082,f6004,f0110,2f0000,12*0,f0082,f6004,f0110,2f0000,12*0,f0082
  //   ,f6004,f0110,2f0000,12*0,f0082,f6004,f0110,2f0000,12*0,f0082,f6004
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  //   32位冯·诺依曼结构微程序控制计算机
  //   contents of ROM (hex, n*v repeats v):
  //   f16,2000000,15,91919191,315,41c64e6d,415,3039,515,10,113,1000000
  //   ,1002f,200031,1f,1f0f35,1a,3f0f35,15,30,a,a15,bbbbbbbb,a0014,1000001
  //   ,f0f36,a15,aaaaaaaa,a0014,1000001,f0f36,a15,ffffffff,a0014,1000001
  //   ,b0b22,b0014,1000002,115,0,10014,1000000,f0f34,2e,30,a,30024,4020
  //   ,5026,f0f36
endmodule
